# Fritzing sketch Schematic v3 - Two Piece (saved by Fritzing 0.7.12b)
breadboards: 1

parts:
  Sen_+5V = Screw terminal - 2 pins [package=THT]
  Sensor_Outputs = screw terminal, 6 pins
  Vin_+12V = Screw terminal - 2 pins [package=THT]
  C1 = Electrolytic Capacitor [capacitance=4.7µF package="200 mil [THT, electrolytic]"]
  5th = mystery part, 3 pins [chip_label=A3144]
  3rd = mystery part, 3 pins [chip_label=A3144]
  1st = mystery part, 3 pins [chip_label=A3144]
  2nd = mystery part, 3 pins [chip_label=A3144]
  4th = mystery part, 3 pins [chip_label=A3144]
  Rev = mystery part, 3 pins [chip_label=A3144]
  Link = screw terminal, 5 pins

nets:
  N1: Sen_+5V.pin1, C1.+, 5th.pin1, 3rd.pin1, 1st.pin1, 2nd.pin1, 4th.pin1, Rev.pin1, Link.pin1
  GND: Sen_+5V.pin2, Vin_+12V.pin2, C1.-, 5th.pin2, 3rd.pin2, 1st.pin2, 2nd.pin2, 4th.pin2, Rev.pin2, Link.pin2
  N2: Sensor_Outputs.pin1, 1st.pin3
  N3: Sensor_Outputs.pin2, 2nd.pin3, Link.pin5
  N4: Sensor_Outputs.pin3, 3rd.pin3
  N5: Sensor_Outputs.pin4, 4th.pin3, Link.pin4
  N6: Sensor_Outputs.pin5, 5th.pin3
  N7: Sensor_Outputs.pin6, Rev.pin3, Link.pin3

notes:
  +
  -
  1
  2
  3
  4
  5
  R
