# Fritzing sketch Schematic v4 - Two Piece (Closer) (saved by Fritzing 0.9.2b)
circuit board: 6cm x 1.5cm
circuit board: 6cm x 1.1cm
breadboards: 1

parts:
  +5V = Screw terminal - 2 pins [package=THT]
  Sensor_Outputs = screw terminal, 6 pins
  C1 = Electrolytic Capacitor [capacitance=4.7µF package="200 mil [THT, electrolytic]"]
  Link = screw terminal, 5 pins
  5th = Mystery Part - 3 pins [chip_label=A3144 package=THT]
  3rd = Mystery Part - 3 pins [chip_label=A3144 package=THT]
  1st = Mystery Part - 3 pins [chip_label=A3144 package=THT]
  Rev = Mystery Part - 3 pins [chip_label=A3144 package=THT]
  4th = Mystery Part - 3 pins [chip_label=A3144 package=THT]
  2nd = Mystery Part - 3 pins [chip_label=A3144 package=THT]
  C2 = Electrolytic Capacitor [capacitance=1µF package="100 mil [THT, electrolytic]"]
  C3 = Ceramic Capacitor [capacitance=100nF package="1206 [SMD, multilayer]"]

nets:
  VCC: +5V.pin1, C1.+, Link.pin1, 5th.Vcc, 3rd.Vcc, 1st.Vcc, Rev.Vcc, 4th.Vcc, 2nd.Vcc, C2.+, C3.1
  GND: +5V.pin2, C1.-, Link.pin2, 5th.GND, 3rd.GND, 1st.GND, Rev.GND, 4th.GND, 2nd.GND, C2.-, C3.0
  N1: Sensor_Outputs.pin1, 1st.Output
  N2: Sensor_Outputs.pin2, Link.pin5, 2nd.Output
  N3: Sensor_Outputs.pin3, 3rd.Output
  N4: Sensor_Outputs.pin4, Link.pin4, 4th.Output
  N5: Sensor_Outputs.pin5, 5th.Output
  N6: Sensor_Outputs.pin6, Link.pin3, Rev.Output

notes:
  +
  -
  1
  2
  3
  4
  5
  R

custom parts:
  Mystery Part - 3 pins: A dummy, proxy, ersatz, stand-in part for whatever you want. With 3 pins on a 100 mil inline pin header footprint.
