# Fritzing sketch Schematic v4 - Two Piece (tight) (saved by Fritzing 0.9.2b)
circuit board: 7cm x 1cm
circuit board: 7cm x 1cm
breadboards: 1

parts:
  Vsen = Screw terminal - 2 pins [package=THT]
  Sensor_Outputs = screw terminal, 6 pins
  Vin = Screw terminal - 2 pins [package=THT]
  C1 = Electrolytic Capacitor [capacitance=4.7µF package="200 mil [THT, electrolytic]"]
  Link = screw terminal, 5 pins
  1st = A3144 Hall Effect [chip_label=A3144 package=THT]
  3rd = A3144 Hall Effect [chip_label=A3144 package=THT]
  5th = A3144 Hall Effect [chip_label=A3144 package=THT]
  2nd = A3144 Hall Effect [chip_label=A3144 package=THT]
  4th = A3144 Hall Effect [chip_label=A3144 package=THT]
  Rev = A3144 Hall Effect [chip_label=A3144 package=THT]

nets:
  VCC: Vsen.pin1, C1.+, Link.pin1, 1st.Vcc, 3rd.Vcc, 5th.Vcc, 2nd.Vcc, 4th.Vcc, Rev.Vcc
  GND: Vsen.pin2, Vin.pin2, C1.-, Link.pin2, 1st.GND, 3rd.GND, 5th.GND, 2nd.GND, 4th.GND, Rev.GND
  N1: Sensor_Outputs.pin1, 1st.Output
  N2: Sensor_Outputs.pin2, Link.pin5, 2nd.Output
  N3: Sensor_Outputs.pin3, 3rd.Output
  N4: Sensor_Outputs.pin4, Link.pin4, 4th.Output
  N5: Sensor_Outputs.pin5, 5th.Output
  N6: Sensor_Outputs.pin6, Link.pin3, Rev.Output

notes:
  +
  -
  1
  2
  3
  4
  5
  R

custom parts:
  A3144 Hall Effect: A dummy, proxy, ersatz, stand-in part for whatever you want. With 3 pins on a 100 mil inline pin header footprint.
