# Fritzing sketch Schematic v1 (saved by Fritzing 0.7.11b)
breadboards: 1

parts:
  Mode = Pushbutton [package="[THT]"]
  Down_(-) = Pushbutton [package="[THT]"]
  Up_(+) = Pushbutton [package="[THT]"]
  Hall_Effect_3rd_Gear = LM35 Temperature Sensor [package="TO92 [THT]"]
  Hall_Effect_1st_Gear = LM35 Temperature Sensor [package="TO92 [THT]"]
  Hall_Effect_5th_Gear = LM35 Temperature Sensor [package="TO92 [THT]"]
  Hall_Effect_2nd_Gear = LM35 Temperature Sensor [package="TO92 [THT]"]
  Hall_Effect_4th_Gear = LM35 Temperature Sensor [package="TO92 [THT]"]
  Hall_Effect_Reverse = LM35 Temperature Sensor [package="TO92 [THT]"]
  Hall_Effect_Signals = screw terminal, 6 pins
  Hall_Effect_Power = Screw terminal - 2 pins [package=THT]
  DC_Power1 = DC Power [voltage=5]
  DC_Power2 = DC Power [voltage=5]
  DC_Power3 = DC Power [voltage=5]
  DC_Power4 = DC Power [voltage=5]
  Power_Input = Screw terminal - 2 pins [package=THT]
  LCD_Contrast = Rotary Potentiometer (Large) [maximum_resistance=10kΩ package=THT]
  VR7809 = Voltage Regulator - 5V [package="TO220 [THT]"]
  C1_100uF = Electrolytic Capacitor [capacitance=10µF package="100 mil [THT, electrolytic]"]
  C2_10uF = Electrolytic Capacitor [capacitance=0.1mF package="100 mil [THT, electrolytic]"]
  Regulator_Pad = Pad [width=15.1545392183908 height=19.3502036704981 connect=center]
  LED = LED - 3mm [color="Green (570nm)" package="3 mm [THT]"]
  R1 = Resistor [tolerance=±5% resistance=330 package=THT]
  16x2_LCD = LCD screen
  Arduino = Arduino

nets:
  GND: Mode.Pin_1, Mode.Pin_2, Down_(-).Pin_1, Down_(-).Pin_2, Up_(+).Pin_1, Up_(+).Pin_2, Hall_Effect_3rd_Gear.GND, Hall_Effect_1st_Gear.GND, Hall_Effect_5th_Gear.GND, Hall_Effect_2nd_Gear.GND, Hall_Effect_4th_Gear.GND, Hall_Effect_Reverse.GND, Hall_Effect_Power.pin2, Power_Input.pin2, LCD_Contrast.leg1, VR7809.GND, C1_100uF.-, C2_10uF.-, Regulator_Pad.pad, LED.cathode, 16x2_LCD.VSS, 16x2_LCD.R/W, 16x2_LCD.LED-, Arduino.GND
  N1: Mode.Pin_3, Mode.Pin_4, Arduino.D10
  N2: Down_(-).Pin_3, Down_(-).Pin_4, Arduino.D12
  N3: Up_(+).Pin_3, Up_(+).Pin_4, Arduino.D11
  VDD: Hall_Effect_3rd_Gear.+Vs, Hall_Effect_1st_Gear.+Vs, Hall_Effect_5th_Gear.+Vs, Hall_Effect_2nd_Gear.+Vs, Hall_Effect_4th_Gear.+Vs, Hall_Effect_Reverse.+Vs, Hall_Effect_Power.pin1, DC_Power1.V+, DC_Power2.V+, DC_Power3.V+, DC_Power4.V+, LCD_Contrast.leg2, 16x2_LCD.VDD, Arduino.+5V
  N4: Hall_Effect_3rd_Gear.Vout, Hall_Effect_Signals.pin3, Arduino.A2
  N5: Hall_Effect_1st_Gear.Vout, Hall_Effect_Signals.pin1, Arduino.A0
  N6: Hall_Effect_5th_Gear.Vout, Hall_Effect_Signals.pin5, Arduino.A4
  N7: Hall_Effect_2nd_Gear.Vout, Hall_Effect_Signals.pin2, Arduino.A1
  N8: Hall_Effect_4th_Gear.Vout, Hall_Effect_Signals.pin4, Arduino.A3
  N9: Hall_Effect_Reverse.Vout, Hall_Effect_Signals.pin6, Arduino.A5
  N10: Power_Input.pin1, VR7809.input_voltage, C1_100uF.+
  N11: LCD_Contrast.wiper, 16x2_LCD.V0
  N12: VR7809.output_voltage, C2_10uF.+, Arduino.VIN
  N13: LED.anode, R1.Pin_0
  N14: R1.Pin_1, Arduino.D2
  N15: 16x2_LCD.RS, Arduino.D9
  N16: 16x2_LCD.E, Arduino.D8
  N17: 16x2_LCD.DB4, Arduino.D7
  N18: 16x2_LCD.DB5, Arduino.D6
  N19: 16x2_LCD.DB6, Arduino.D5
  N20: 16x2_LCD.DB7, Arduino.D4
  N21: 16x2_LCD.LED+, Arduino.D3

notes:
  Manual Transmission Shifter Shaft Here (Magnetized)
  Mode
  1st
  2nd
  3rd
  4th
  5th
  Reverse
  LCD Contrast
  Down
  Up
  Gear Display v1
  Gear
  By Eric Menze
  v1 1.13.2013
  min 11VDC
  max 20VDC
  +
  -
  Rev
  Arduino
  Display v1
  Code available at www.github.com/Ehryk
  330Ω
  Liquid Crystal Display
  16x2 LCD Display
  LED
  Regulate Vehicle Voltage 11.5V - 14.4V to 9V
  Vehicle Voltage In
  Sensor Inputs
  Sensor Power
  Shifter Here
  Gear Display Shield
  <- 8+ Conductor->
  (magnetized)
  Cable
