# Fritzing sketch Schematic (saved by Fritzing 0.7.11b)
breadboards: 1

parts:
  Arduino = Arduino
  Mode = Pushbutton [package="[THT]"]
  Down_(-) = Pushbutton [package="[THT]"]
  Up_(+) = Pushbutton [package="[THT]"]
  Hall_Effect_3rd_Gear = LM35 Temperature Sensor [package="TO92 [THT]"]
  Hall_Effect_1st_Gear = LM35 Temperature Sensor [package="TO92 [THT]"]
  Hall_Effect_5th_Gear = LM35 Temperature Sensor [package="TO92 [THT]"]
  Hall_Effect_2nd_Gear = LM35 Temperature Sensor [package="TO92 [THT]"]
  Hall_Effect_4th_Gear = LM35 Temperature Sensor [package="TO92 [THT]"]
  Hall_Effect_Reverse = LM35 Temperature Sensor [package="TO92 [THT]"]
  Hall_Effect_Signals = screw terminal, 6 pins
  Hall_Effect_Power = Screw terminal - 2 pins [package=THT]
  DC_Power1 = DC Power [voltage=5]
  DC_Power2 = DC Power [voltage=5]
  DC_Power3 = DC Power [voltage=5]
  DC_Power4 = DC Power [voltage=5]
  Power_Input = Screw terminal - 2 pins [package=THT]
  LCD_Contrast = Rotary Potentiometer (Large) [maximum_resistance=10kΩ package=THT]
  VR7809 = Voltage Regulator - 5V [package="TO220 [THT]"]
  C1_100uF = Electrolytic Capacitor [capacitance=10µF package="100 mil [THT, electrolytic]"]
  C2_10uF = Electrolytic Capacitor [capacitance=0.1mF package="100 mil [THT, electrolytic]"]
  16x2_LCD = LCD screen
  Regulator_Pad = Pad [width=7.90222222222222 height=9.03111111111111 connect=center]
  LED = LED - 3mm [color="Green (570nm)" package="3 mm [THT]"]
  R1 = Resistor [tolerance=±5% resistance=330 package=THT]

nets:
  GND: Arduino.GND, Mode.Pin_1, Mode.Pin_2, Down_(-).Pin_1, Down_(-).Pin_2, Up_(+).Pin_1, Up_(+).Pin_2, Hall_Effect_3rd_Gear.GND, Hall_Effect_1st_Gear.GND, Hall_Effect_5th_Gear.GND, Hall_Effect_2nd_Gear.GND, Hall_Effect_4th_Gear.GND, Hall_Effect_Reverse.GND, Hall_Effect_Power.pin2, Power_Input.pin2, LCD_Contrast.leg1, VR7809.GND, C1_100uF.-, C2_10uF.-, 16x2_LCD.VSS, 16x2_LCD.R/W, Regulator_Pad.pad, LED.cathode
  N1: Arduino.D12, 16x2_LCD.RS
  N2: Arduino.D11, 16x2_LCD.E
  N3: Arduino.D10, Down_(-).Pin_3, Down_(-).Pin_4
  N4: Arduino.D9, Up_(+).Pin_3, Up_(+).Pin_4
  N5: Arduino.D8, Mode.Pin_3, Mode.Pin_4
  N6: Arduino.D5, 16x2_LCD.DB4
  N7: Arduino.D4, 16x2_LCD.DB5
  N8: Arduino.D3, 16x2_LCD.DB6
  N9: Arduino.D2, 16x2_LCD.DB7
  N10: Arduino.D0RX, R1.Pin_1
  +5V: Arduino.+5V, Hall_Effect_3rd_Gear.+Vs, Hall_Effect_1st_Gear.+Vs, Hall_Effect_5th_Gear.+Vs, Hall_Effect_2nd_Gear.+Vs, Hall_Effect_4th_Gear.+Vs, Hall_Effect_Reverse.+Vs, Hall_Effect_Power.pin1, DC_Power1.V+, DC_Power2.V+, DC_Power3.V+, DC_Power4.V+, LCD_Contrast.leg2, 16x2_LCD.VDD
  N11: Arduino.VIN, VR7809.output_voltage, C2_10uF.+
  N12: Arduino.A0, Hall_Effect_1st_Gear.Vout, Hall_Effect_Signals.pin1
  N13: Arduino.A1, Hall_Effect_2nd_Gear.Vout, Hall_Effect_Signals.pin2
  N14: Arduino.A2, Hall_Effect_3rd_Gear.Vout, Hall_Effect_Signals.pin3
  N15: Arduino.A3, Hall_Effect_4th_Gear.Vout, Hall_Effect_Signals.pin4
  N16: Arduino.A4, Hall_Effect_5th_Gear.Vout, Hall_Effect_Signals.pin5
  N17: Arduino.A5, Hall_Effect_Reverse.Vout, Hall_Effect_Signals.pin6
  N18: Power_Input.pin1, VR7809.input_voltage, C1_100uF.+
  N19: LCD_Contrast.wiper, 16x2_LCD.V0
  N20: LED.anode, R1.Pin_0

notes:
  Manual Transmission Shifter Shaft Here (Magnetized)
  Mode
  1st
  2nd
  3rd
  4th
  5th
  Reverse
  Contrast
  Down
  Up
  Gear Display v1
  Gear
  By Eric Menze
  v1 1.13.2013
  min 11VDC
  max 20VDC
  +
  -
  Rev
  Arduino
  Display v1
  Code available at www.github.com/Ehryk
  330Ω
  Liquid Crystal Display
