# Fritzing sketch Schematic v1.1 - For Casing (saved by Fritzing 0.7.11b)
breadboards: 1

parts:
  Mode = Pushbutton [package="[THT]"]
  Down_(-) = Pushbutton [package="[THT]"]
  Up_(+) = Pushbutton [package="[THT]"]
  Hall_Effect_3rd_Gear = LM35 Temperature Sensor [package="TO92 [THT]"]
  Hall_Effect_1st_Gear = LM35 Temperature Sensor [package="TO92 [THT]"]
  Hall_Effect_5th_Gear = LM35 Temperature Sensor [package="TO92 [THT]"]
  Hall_Effect_2nd_Gear = LM35 Temperature Sensor [package="TO92 [THT]"]
  Hall_Effect_4th_Gear = LM35 Temperature Sensor [package="TO92 [THT]"]
  Hall_Effect_Reverse = LM35 Temperature Sensor [package="TO92 [THT]"]
  Hall_Effect_Signals = screw terminal, 6 pins
  Hall_Effect_Power = Screw terminal - 2 pins [package=THT]
  DC_Power1 = DC Power [voltage=5]
  DC_Power2 = DC Power [voltage=5]
  DC_Power3 = DC Power [voltage=5]
  DC_Power4 = DC Power [voltage=5]
  Power_Input = Screw terminal - 2 pins [package=THT]
  VR7809 = Voltage Regulator - 5V [package="TO220 [THT]"]
  C_input_100uF = Electrolytic Capacitor [capacitance=10µF package="100 mil [THT, electrolytic]"]
  C_output_10uF = Electrolytic Capacitor [capacitance=0.1mF package="100 mil [THT, electrolytic]"]
  LED = LED - 3mm [color="Green (570nm)" package="3 mm [THT]"]
  R1 = Resistor [tolerance=±5% resistance=330 package=THT]
  16x2_LCD = LCD screen
  LCD_Contrast = Rotary Potentiometer (Small) [maximum_resistance=10kΩ]
  Regulator_Pad = Pad [width=14.9881246267806 height=16.5447372136752 connect=center]
  Rcharge = Resistor [tolerance=±5% resistance=10 package=THT]
  Duc = Schottky Diode [part_number=1N5817 package="300 mil [THT]"]
  UC1 = Electrolytic Capacitor [capacitance=4.7mF package="300 mil [THT, electrolytic]"]
  Arduino = Arduino
  Jard = Resistor [tolerance=±5% resistance=0 package="0805 [SMD]"]
  Jvin = Resistor [tolerance=±5% resistance=0 package="0805 [SMD]"]
  Q1 = NPN-Transistor [package="TO92 [THT]"]

nets:
  GND: Mode.Pin_1, Mode.Pin_2, Down_(-).Pin_1, Down_(-).Pin_2, Up_(+).Pin_1, Up_(+).Pin_2, DC_Power1.GND, DC_Power2.GND, DC_Power3.GND, DC_Power4.GND, Power_Input.pin2, VR7809.GND, C_input_100uF.-, C_output_10uF.-, LED.cathode, 16x2_LCD.VSS, 16x2_LCD.R/W, 16x2_LCD.LED-, LCD_Contrast.leg1, Regulator_Pad.pad, UC1.-, Arduino.GND, Q1.E
  N1: Mode.Pin_3, Mode.Pin_4, Arduino.D2
  N2: Down_(-).Pin_3, Down_(-).Pin_4, Arduino.D0RX
  N3: Up_(+).Pin_3, Up_(+).Pin_4, Arduino.D1TX
  N4: Hall_Effect_3rd_Gear.+Vs, Hall_Effect_1st_Gear.+Vs, Hall_Effect_5th_Gear.+Vs, Hall_Effect_2nd_Gear.+Vs, Hall_Effect_4th_Gear.+Vs, Hall_Effect_Reverse.+Vs, Hall_Effect_Power.pin1, Jard.Pin_0, Jvin.Pin_0
  N5: Hall_Effect_3rd_Gear.Vout, Hall_Effect_Signals.pin3, Arduino.A2
  GND_2: Hall_Effect_3rd_Gear.GND, Hall_Effect_1st_Gear.GND, Hall_Effect_5th_Gear.GND, Hall_Effect_2nd_Gear.GND, Hall_Effect_4th_Gear.GND, Hall_Effect_Reverse.GND, Hall_Effect_Power.pin2, Q1.C
  N6: Hall_Effect_1st_Gear.Vout, Hall_Effect_Signals.pin1, Arduino.A0
  N7: Hall_Effect_5th_Gear.Vout, Hall_Effect_Signals.pin5, Arduino.A4
  N8: Hall_Effect_2nd_Gear.Vout, Hall_Effect_Signals.pin2, Arduino.A1
  N9: Hall_Effect_4th_Gear.Vout, Hall_Effect_Signals.pin4, Arduino.A3
  N10: Hall_Effect_Reverse.Vout, Hall_Effect_Signals.pin6, Arduino.A5
  VDD: DC_Power1.V+, DC_Power2.V+, DC_Power3.V+, DC_Power4.V+, 16x2_LCD.VDD, LCD_Contrast.leg2, Rcharge.Pin_0, Duc.cathode, Arduino.+5V, Jvin.Pin_1
  N11: Power_Input.pin1, VR7809.input_voltage, C_input_100uF.+
  N12: VR7809.output_voltage, C_output_10uF.+, Arduino.VIN
  N13: LED.anode, R1.Pin_0
  N14: R1.Pin_1, Arduino.D5
  N15: 16x2_LCD.V0, LCD_Contrast.wiper
  N16: 16x2_LCD.RS, Arduino.D7
  N17: 16x2_LCD.E, Arduino.D8
  N18: 16x2_LCD.DB4, Arduino.D12
  N19: 16x2_LCD.DB5, Arduino.D11
  N20: 16x2_LCD.DB6, Arduino.D10
  N21: 16x2_LCD.DB7, Arduino.D9
  N22: 16x2_LCD.LED+, Arduino.D6
  N23: Rcharge.Pin_1, Duc.anode, UC1.+
  N24: Arduino.D4, Jard.Pin_1, Q1.B

notes:
  Manual Transmission Shifter Shaft Here (Magnetized)
  Mode
  1st
  2nd
  3rd
  4th
  5th
  Reverse
  LCD Contrast
  Down
  Up
  Gear Display v1.1
  By Eric Menze
  v1.1 1.27.2013
  min 11VDC
  max 20VDC
  +
  -
  Rev
  GND
  +9V
  Code available at www.github.com/Ehryk
  330Ω
  Liquid Crystal Display
  Arduino
  16x2 LCD Display
  LED
  Regulate Vehicle Voltage 11.5V - 14.4V to 9V
  Vehicle Voltage In
  Sensor Inputs
  Sensor Power
  Shifter Here
  Gear Display LCD Shield
  <- 8+ Conductor->
  (magnetized)
  Cable
  VIN
  Ultra
  Capacitor
  .22F
  10KΩ
