# Fritzing sketch Schematic v3 (saved by Fritzing 0.9.3b)
circuit board: 8cm x 6cm
breadboards: 1

parts:
  Mode = Pushbutton [package="[THT]"]
  Down_(-) = Pushbutton [package="[THT]"]
  Up_(+) = Pushbutton [package="[THT]"]
  Hall_Effect_1st_Gear = LM35 Temperature Sensor [package="TO92 [THT]"]
  Hall_Effect_5th_Gear = LM35 Temperature Sensor [package="TO92 [THT]"]
  Hall_Effect_2nd_Gear = LM35 Temperature Sensor [package="TO92 [THT]"]
  Hall_Effect_4th_Gear = LM35 Temperature Sensor [package="TO92 [THT]"]
  Hall_Effect_Reverse = LM35 Temperature Sensor [package="TO92 [THT]"]
  Gears = screw terminal, 6 pins
  SEN_PWR = Screw terminal - 2 pins [package=THT]
  Power_In = Screw terminal - 2 pins [package=THT]
  Cinput = Electrolytic Capacitor [capacitance=10µF voltage=35V package="100 mil [THT, electrolytic]"]
  Coutput = Electrolytic Capacitor [capacitance=0.1mF voltage=16V package="100 mil [THT, electrolytic]"]
  LED = LED - 3mm [color="Green (570nm)" package="3 mm [THT]"]
  Rled = Resistor [tolerance=±5% resistance=330 package=THT]
  16x2_LCD = LCD screen
  Regulator_Pad = Pad [width=17.8103106666667 height=19.9314030909091 connect=center]
  Rcharge = Resistor [tolerance=±5% resistance=10 package=THT]
  Duc = Schottky Diode [part_number=1N5817 package="300 mil [THT]"]
  UC1 = Electrolytic Capacitor [capacitance=4.7mF package="300 mil [THT, electrolytic]"]
  (Jino) = Resistor [tolerance=±5% resistance=0 package="0805 [SMD]"]
  (J5v) = Resistor [tolerance=±5% resistance=0 package="0805 [SMD]"]
  MC14490 = IC, DIP package, 16 pins [chip_label=MC14990]
  Jm = Resistor [tolerance=±5% resistance=0 package="0805 [SMD]"]
  J+ = Resistor [tolerance=±5% resistance=0 package="0805 [SMD]"]
  J- = Resistor [tolerance=±5% resistance=0 package="0805 [SMD]"]
  Dclamp = Zener Diode [part_number=1N4732A breakdown_voltage=9.1V package="300 mil [THT]"]
  Cosc = Electrolytic Capacitor [capacitance="1 μF" package="100 mil [THT, electrolytic]"]
  Qsenpwr = NPN-Transistor [package="TO92 [THT]"]
  Arduino = Arduino Uno (Rev3)
  VR7809 = Voltage Regulator - 5V [part_number="7809 9V" package="TO220 [THT]"]
  Hall_Effect_3rd_Gear = LM35 Temperature Sensor [package="TO92 [THT]"]
  LCD_Contrast = Trimmer Potentiometer [maximum_resistance=10kΩ package=THT]
  Rsenpwr = Resistor [tolerance=±5% resistance=1k package=THT]

nets:
  GND: Mode.Pin_1, Mode.Pin_2, Down_(-).Pin_1, Down_(-).Pin_2, Up_(+).Pin_1, Up_(+).Pin_2, Power_In.pin2, Cinput.-, Coutput.-, LED.cathode, 16x2_LCD.VSS, 16x2_LCD.R/W, 16x2_LCD.DB0, 16x2_LCD.DB1, 16x2_LCD.DB2, 16x2_LCD.DB3, 16x2_LCD.LED-, Regulator_Pad.pad, UC1.-, MC14490.pin8, MC14490.pin10, MC14490.pin12, MC14490.pin14, Dclamp.anode, Qsenpwr.E, Arduino.GND, VR7809.GND, LCD_Contrast.leg2
  N1: Mode.Pin_3, Mode.Pin_4, MC14490.pin1, Jm.Pin_0
  N2: Down_(-).Pin_3, Down_(-).Pin_4, MC14490.pin5, J-.Pin_0
  N3: Up_(+).Pin_3, Up_(+).Pin_4, MC14490.pin3, J+.Pin_0
  SEN+: Hall_Effect_1st_Gear.+Vs, Hall_Effect_5th_Gear.+Vs, Hall_Effect_2nd_Gear.+Vs, Hall_Effect_4th_Gear.+Vs, Hall_Effect_Reverse.+Vs, SEN_PWR.pin1, (Jino).Pin_1, (J5v).Pin_1, Hall_Effect_3rd_Gear.+Vs
  GEAR_1: Hall_Effect_1st_Gear.Vout, Gears.pin1, Arduino.A0
  SEN-: Hall_Effect_1st_Gear.GND, Hall_Effect_5th_Gear.GND, Hall_Effect_2nd_Gear.GND, Hall_Effect_4th_Gear.GND, Hall_Effect_Reverse.GND, SEN_PWR.pin2, Qsenpwr.C, Hall_Effect_3rd_Gear.GND
  GEAR_5: Hall_Effect_5th_Gear.Vout, Gears.pin5, Arduino.A4/SDA
  GEAR_2: Hall_Effect_2nd_Gear.Vout, Gears.pin2, Arduino.A1
  GEAR_4: Hall_Effect_4th_Gear.Vout, Gears.pin4, Arduino.A3
  GEAR_R: Hall_Effect_Reverse.Vout, Gears.pin6, Arduino.A5/SCL
  GEAR_3: Gears.pin3, Arduino.A2, Hall_Effect_3rd_Gear.Vout
  12V: Power_In.pin1, Cinput.+, VR7809.input_voltage
  9V: Coutput.+, Dclamp.cathode, Arduino.VIN, VR7809.output_voltage
  N4: LED.anode, Rled.Pin_0
  LED: Rled.Pin_1, Arduino.D5_PWM
  5V: 16x2_LCD.VDD, Rcharge.Pin_0, Duc.cathode, (J5v).Pin_0, MC14490.pin16, Arduino.5V, LCD_Contrast.leg1
  LCD_Contrast: 16x2_LCD.V0, LCD_Contrast.wiper
  LCD_RS: 16x2_LCD.RS, Arduino.D7
  LCD_Enable: 16x2_LCD.E, Arduino.D8
  LCD_D4: 16x2_LCD.DB4, Arduino.D12/MISO
  LCD_D5: 16x2_LCD.DB5, Arduino.D11_PWM/MOSI
  LCD_D6: 16x2_LCD.DB6, Arduino.D10_PWM/SS
  LCD_D7: 16x2_LCD.DB7, Arduino.D9_PWM
  LCD_Brightness: 16x2_LCD.LED+, Arduino.D6_PWM
  N5: Rcharge.Pin_1, Duc.anode, UC1.+
  SEN_PWR: (Jino).Pin_0, Arduino.D4, Rsenpwr.Pin_0
  N6: MC14490.pin7, Cosc.+
  N7: MC14490.pin9, Cosc.-
  B_Down: MC14490.pin11, J-.Pin_1, Arduino.D2
  B_Up: MC14490.pin13, J+.Pin_1, Arduino.D3_PWM
  B_Mode: MC14490.pin15, Jm.Pin_1, Arduino.D13/SCK
  N8: Qsenpwr.B, Rsenpwr.Pin_1

notes:
  Manual Transmission Shifter Shaft Here (Magnetized)
  Mode
  1st
  2nd
  3rd
  4th
  5th
  Reverse
  LCD Contrast
  Down
  Up
  min 11VDC
  max 20VDC
  +
  -
  Rev
  GND
  +9V
  Gear Display v3
  By Eric Menze
  330Ω
  v3 10.6.2016
  16x2 LCD Display
  Arduino UNO
  LED
  Regulate Vehicle Voltage
  11.5V - 14.4V to 9V
  Vehicle Voltage In
  Sensor Inputs
  Sensor Power
  Shifter Here
  Gear Display LCD Shield
  <- 8+ Conductor->
  (magnetized)
  Cable
  VIN
  Arduino
  Ultra
  Capacitor
  .22F
  10KΩ
  Input
  Output
  Vehicle Power
  Keep Alive Circuit
  Sensor Signals
  Gear Sensors
  www.github.com/Ehryk/GearDisplay
