# Fritzing sketch Schematic v3 (saved by Fritzing 0.7.11b)
breadboards: 1

parts:
  Hall_Effect_3rd_Gear = LM35 Temperature Sensor [package="TO92 [THT]"]
  Hall_Effect_1st_Gear = LM35 Temperature Sensor [package="TO92 [THT]"]
  Hall_Effect_5th_Gear = LM35 Temperature Sensor [package="TO92 [THT]"]
  Hall_Effect_2nd_Gear = LM35 Temperature Sensor [package="TO92 [THT]"]
  Hall_Effect_4th_Gear = LM35 Temperature Sensor [package="TO92 [THT]"]
  Hall_Effect_Reverse = LM35 Temperature Sensor [package="TO92 [THT]"]
  HE_Signals = screw terminal, 6 pins
  HE_Power = Screw terminal - 2 pins [package=THT]
  DC_Power1 = DC Power [voltage=5]
  DC_Power4 = DC Power [voltage=5]
  Power_Input = Screw terminal - 2 pins [package=THT]
  VR7809 = Voltage Regulator - 5V [package="TO220 [THT]"]
  C_input_100uF = Electrolytic Capacitor [capacitance=10µF package="100 mil [THT, electrolytic]"]
  C_output_10uF = Electrolytic Capacitor [capacitance=0.1mF package="100 mil [THT, electrolytic]"]
  LED = LED - 3mm [color="Green (570nm)" package="3 mm [THT]"]
  R1 = Resistor [tolerance=±5% resistance=330 package=THT]
  Regulator_Pad = Pad [width=14.9881246267806 height=16.5447372136752 connect=center]  # not connected
  Rcharge = Resistor [tolerance=±5% resistance=10 package=THT]
  Duc = Schottky Diode [part_number=1N5817 package="300 mil [THT]"]
  UC1 = Electrolytic Capacitor [capacitance=4.7mF package="300 mil [THT, electrolytic]"]
  Arduino = Arduino
  Jard = Resistor [tolerance=±5% resistance=0 package="0805 [SMD]"]
  Jvin = Resistor [tolerance=±5% resistance=0 package="0805 [SMD]"]
  Q1 = NPN-Transistor [package="TO92 [THT]"]
  TFT_Touchscreen2 = TFT Color Touchscreen [chip_label="TFT Touchscreen" package="DIP (Dual Inline) [THT]"]  # not connected

nets:
  N1: Hall_Effect_3rd_Gear.+Vs, Hall_Effect_1st_Gear.+Vs, Hall_Effect_5th_Gear.+Vs, Hall_Effect_2nd_Gear.+Vs, Hall_Effect_4th_Gear.+Vs, Hall_Effect_Reverse.+Vs, HE_Power.pin1, Arduino.D2, Jard.Pin_0, Jard.Pin_1, Jvin.Pin_0, Q1.B
  N2: Hall_Effect_3rd_Gear.Vout, HE_Signals.pin3, Arduino.A2
  GND: Hall_Effect_3rd_Gear.GND, Hall_Effect_1st_Gear.GND, Hall_Effect_5th_Gear.GND, Hall_Effect_2nd_Gear.GND, Hall_Effect_4th_Gear.GND, Hall_Effect_Reverse.GND, HE_Power.pin2, Q1.C
  N3: Hall_Effect_1st_Gear.Vout, HE_Signals.pin1, Arduino.A0
  N4: Hall_Effect_5th_Gear.Vout, HE_Signals.pin5, Arduino.A4
  N5: Hall_Effect_2nd_Gear.Vout, HE_Signals.pin2, Arduino.A1
  N6: Hall_Effect_4th_Gear.Vout, HE_Signals.pin4, Arduino.A3
  N7: Hall_Effect_Reverse.Vout, HE_Signals.pin6, Arduino.A5
  N8: DC_Power1.V+, DC_Power4.V+, Rcharge.Pin_0, Duc.cathode, Arduino.+5V, Jvin.Pin_1
  GND_2: DC_Power1.GND, DC_Power4.GND, Power_Input.pin2, VR7809.GND, C_input_100uF.-, C_output_10uF.-, LED.cathode, UC1.-, Arduino.GND, Q1.E
  N9: Power_Input.pin1, VR7809.input_voltage, C_input_100uF.+
  N10: VR7809.output_voltage, C_output_10uF.+, Arduino.VIN
  N11: LED.anode, R1.Pin_0
  N12: R1.Pin_1, Arduino.D3
  N13: Rcharge.Pin_1, Duc.anode, UC1.+

notes:
  Manual Transmission Shifter Shaft Here (Magnetized)
  1st
  2nd
  3rd
  4th
  5th
  Reverse
  Gear Display v3
  By Eric Menze
  v3 1.30.2013
  min 11VDC
  max 20VDC
  +
  -
  Rev
  GND
  +9V
  Code available at www.github.com/Ehryk
  330Ω
  Arduino
  LED
  Regulate Vehicle Voltage 11.5V - 14.4V to 9V
  Vehicle Voltage In
  Sensor Inputs
  Sensor Power
  Shifter Here
  Gear Display LCD Shield
  <- 8+ Conductor->
  (magnetized)
  Cable
  VIN
  Ultra
  Capacitor
  .22F
  10KΩ
