# Fritzing sketch Schematic (saved by Fritzing 0.7.11b)
breadboards: 1

parts:
  Arduino = Arduino
  TFT_40_pin_Touchscreen = IC, DIP package, 40 pins [chip_label=ITDB02_40pins spacing=300mil]
  U2 = Arduino Micro [chip_label="Arduino Nano" package=THT]  # not connected
  TFT_Touchscreen1 = TFT Color Touchscreen [chip_label="TFT Touchscreen" package="DIP (Dual Inline) [THT]"]  # not connected

nets:
  N1: Arduino.D11, TFT_40_pin_Touchscreen.pin17
  N2: Arduino.D10, TFT_40_pin_Touchscreen.pin15
  N3: Arduino.D9, TFT_40_pin_Touchscreen.pin5
  N4: Arduino.D8, TFT_40_pin_Touchscreen.pin4
  N5: Arduino.D7, TFT_40_pin_Touchscreen.pin14
  N6: Arduino.D6, TFT_40_pin_Touchscreen.pin13
  N7: Arduino.D5, TFT_40_pin_Touchscreen.pin12
  N8: Arduino.D4, TFT_40_pin_Touchscreen.pin11
  N9: Arduino.D3, TFT_40_pin_Touchscreen.pin10
  N10: Arduino.D2, TFT_40_pin_Touchscreen.pin9
  N11: Arduino.D1TX, TFT_40_pin_Touchscreen.pin8
  N12: Arduino.D0RX, TFT_40_pin_Touchscreen.pin7
  N13: Arduino.3V3, TFT_40_pin_Touchscreen.pin6, TFT_40_pin_Touchscreen.pin19
  N14: Arduino.+5V, TFT_40_pin_Touchscreen.pin2
  GND: Arduino.GND, TFT_40_pin_Touchscreen.pin1
  N15: Arduino.A0, TFT_40_pin_Touchscreen.pin26
  N16: Arduino.A1, TFT_40_pin_Touchscreen.pin27
  N17: Arduino.A2, TFT_40_pin_Touchscreen.pin28
  N18: Arduino.A3, TFT_40_pin_Touchscreen.pin29
  N19: Arduino.A4, TFT_40_pin_Touchscreen.pin30
  N20: Arduino.A5, TFT_40_pin_Touchscreen.pin31
